# Fritzing sketch schema (saved by Fritzing 0.9.3b)
breadboards: 1

parts:
  Arduino_UNO = Arduino Uno (Rev3)
  callButton1 = Pushbutton [package=THT]
  callButton2 = Pushbutton [package=THT]
  callButton3 = Pushbutton [package=THT]
  elevButton2 = Pushbutton [package=THT]
  elevButton1 = Pushbutton [package=THT]
  elevButton3 = Pushbutton [package=THT]
  callLED1 = LED - 5mm [color="Red (633nm)" package="5 mm [THT]"]
  callLED2 = LED - 5mm [color="Red (633nm)" package="5 mm [THT]"]
  callLED3 = LED - 5mm [color="Red (633nm)" package="5 mm [THT]"]
  R1 = Resistor [tolerance=±5% resistance=220 package=THT]
  R2 = Resistor [tolerance=±5% resistance=220 package=THT]
  R3 = Resistor [tolerance=±5% resistance=220 package=THT]
  elevLED3 = LED - 5mm [color="Red (633nm)" package="5 mm [THT]"]
  elevLED1 = LED - 5mm [color="Red (633nm)" package="5 mm [THT]"]
  elevLED2 = LED - 5mm [color="Red (633nm)" package="5 mm [THT]"]
  R4 = Resistor [tolerance=±5% resistance=220 package=THT]
  R5 = Resistor [tolerance=±5% resistance=220 package=THT]
  R6 = Resistor [tolerance=±5% resistance=220 package=THT]

nets:
  N1: Arduino_UNO.D8, elevButton3.leg0
  N2: Arduino_UNO.D9_PWM, elevLED1.anode
  N3: Arduino_UNO.D10_PWM/SS, elevLED2.anode
  N4: Arduino_UNO.D11_PWM/MOSI, elevLED3.anode
  N5: Arduino_UNO.GND, callButton1.leg1, callButton2.leg1, callButton3.leg1, elevButton2.leg1, elevButton1.leg1, elevButton3.leg1, R1.Pin_1, R2.Pin_1, R3.Pin_1, R4.Pin_1, R5.Pin_1, R6.Pin_1
  N6: Arduino_UNO.D0/RX, callButton1.leg0
  N7: Arduino_UNO.D1/TX, callButton2.leg0
  N8: Arduino_UNO.D2, callButton3.leg0
  N9: Arduino_UNO.D3_PWM, callLED1.anode
  N10: Arduino_UNO.D4, callLED2.anode
  N11: Arduino_UNO.D5_PWM, callLED3.anode
  N12: Arduino_UNO.D6_PWM, elevButton1.leg0
  N13: Arduino_UNO.D7, elevButton2.leg0
  N14: callLED1.cathode, R1.Pin_0
  N15: callLED2.cathode, R2.Pin_0
  N16: callLED3.cathode, R3.Pin_0
  N17: elevLED3.cathode, R6.Pin_0
  N18: elevLED1.cathode, R4.Pin_0
  N19: elevLED2.cathode, R5.Pin_0
